// Logisim project xyazbcd_74.circ as structural Verilog: 4 circuits, main circuit main
module main (
  input  in_1,
  input  in_2,
  input  in_3,
  input  in_4,
  input  X,
  input  Y,
  input  a,
  input  Z,
  input  b,
  input  c,
  input  d,
  output out_12,
  output out_13,
  output out_14,
  output out_15,
  output out_16,
  output out_17,
  output out_18,
  output X_2,
  output Y_2,
  output Z_2
);

  wire corrup_1_out_11, corrup_1_out_12, corrup_1_out_13, corrup_1_out_14, corrup_1_out_15, corrup_1_out_16,
       corrup_1_out_17;

  xyazbcd xyazbcd_1 (
    .a(in_1), .b(in_2), .c(in_3), .d(in_4), .X(out_12), .Y(out_13), .a_2(out_14), .Z(out_15), .b_2(out_16),
    .c_2(out_17), .d_2(out_18));
  corrup corrup_1 (
    .X(X), .Y(Y), .a(a), .Z(Z), .b(b), .c(c), .d(d), .CmpX(X_2), .CmpY(Y_2), .CmpZ(Z_2),
    .out_11(corrup_1_out_11), .out_12(corrup_1_out_12), .out_13(corrup_1_out_13), .out_14(corrup_1_out_14),
    .out_15(corrup_1_out_15), .out_16(corrup_1_out_16), .out_17(corrup_1_out_17));
  _7_Segment_Display u_7_segment_display_1 (
    .g(corrup_1_out_17), .f(corrup_1_out_16), .a(corrup_1_out_15), .b(corrup_1_out_14), .e(corrup_1_out_11),
    .d(corrup_1_out_12), .c(corrup_1_out_13));  // open: dp
endmodule

module xyazbcd (
  input  a,
  input  b,
  input  c,
  input  d,
  output X,
  output Y,
  output a_2,
  output Z,
  output b_2,
  output c_2,
  output d_2
);

  xor xor_1 (X, a, b, d);
  xor xor_2 (Y, a, c, d);
  xor xor_3 (Z, b, c, d);

  assign a_2 = a;
  assign b_2 = b;
  assign c_2 = c;
  assign d_2 = d;
endmodule

module corrup (
  input  X,
  input  Y,
  input  a,
  input  Z,
  input  b,
  input  c,
  input  d,
  output CmpX,
  output CmpY,
  output CmpZ,
  output out_11,
  output out_12,
  output out_13,
  output out_14,
  output out_15,
  output out_16,
  output out_17
);

  wire xor_1_out, xor_2_out, xor_3_out;

  xor xor_1 (xor_1_out, a, b, d);
  xor xor_2 (xor_2_out, a, c, d);
  xor xor_3 (xor_3_out, b, c, d);
  xor xor_4 (CmpX, xor_1_out, X);
  xor xor_5 (CmpY, xor_2_out, Y);
  xor xor_6 (CmpZ, xor_3_out, Z);
  sevenSegment sevensegment_1 (
    .x(CmpX), .y(CmpY), .z(CmpZ), .g1(out_11), .g2(out_12), .g3(out_13), .g4(out_14), .g5(out_15),
    .g6(out_16), .g7(out_17));

  // Notes on the sheet:
  //     2
  //     1
  //     3
  //     4
  //     6
  //     5
  //     7
endmodule

module sevenSegment (
  input  x,
  input  y,
  input  z,
  output g1,
  output g2,
  output g3,
  output g4,
  output g5,
  output g6,
  output g7
);

  wire and_1_out, and_3_out, and_4_out, and_5_out, and_6_out, and_7_out, and_8_out, and_9_out, and_10_out,
       and_11_out, and_12_out, and_13_out, and_14_out, not_1_out, not_2_out, not_3_out, not_4_out, not_5_out,
       not_6_out, not_7_out, not_8_out, not_9_out, not_10_out, not_11_out, not_12_out, not_13_out;

  not not_1 (not_1_out, x);
  not not_2 (not_2_out, x);
  not not_3 (not_3_out, z);
  not not_4 (not_4_out, y);
  or or_1 (g3, z, x);
  not not_5 (not_5_out, x);
  not not_6 (not_6_out, y);
  not not_7 (not_7_out, z);
  not not_8 (not_8_out, z);
  and and_1 (and_1_out, x, z);
  not not_9 (not_9_out, x);
  not not_10 (not_10_out, y);
  not not_11 (not_11_out, y);
  not not_12 (not_12_out, x);
  not not_13 (not_13_out, z);
  and and_2 (g1, not_1_out, y);
  and and_3 (and_3_out, not_2_out, y);
  and and_4 (and_4_out, y, not_3_out);
  and and_5 (and_5_out, x, not_4_out, z);
  and and_6 (and_6_out, not_5_out, not_6_out, z);
  and and_7 (and_7_out, y, not_7_out);
  and and_8 (and_8_out, x, not_8_out);
  and and_9 (and_9_out, x, y);
  or or_2 (g5, y, and_1_out);
  and and_10 (and_10_out, not_9_out, z);
  and and_11 (and_11_out, not_10_out, z);
  and and_12 (and_12_out, not_11_out, z);
  and and_13 (and_13_out, not_12_out, y);
  and and_14 (and_14_out, y, not_13_out);
  or or_3 (g2, and_3_out, and_4_out, and_5_out);
  or or_4 (g4, and_6_out, and_7_out, and_8_out, and_9_out);
  or or_5 (g6, and_10_out, and_11_out);
  or or_6 (g7, and_12_out, and_13_out, and_14_out);
endmodule
